# Fritzing sketch esp32-1-relais (saved by Fritzing 1.0.4)
breadboards: 1

parts:
  U1 = ESP32-38PinWide [part_number=ESP32-38PinWide]
  A2 = 1 chan 3v relay module
  S6 = Round Pushbutton

nets:
  N1: U1.3.3, A2.pin_1
  N2: U1.GND, A2.pin_3
  N3: U1.GPIO13, A2.pin_2
  N4: A2.pin_6, S6.leg1
  N5: A2.pin_7, S6.leg0

custom parts:
  ESP32-38PinWide: Generic 38-Pin ESP32 with wide format (only access to one side of pins on a breadboard) based on Stephen Lilley's HiLetgo ESP-WROOM-32 ESP32 ESP-32S Development Board.
  1 chan 3v relay module: Single 3V relay isolated drive control module High level drive board.
