# Fritzing sketch esp32-3-relais (saved by Fritzing 1.0.4)
breadboards: 1

parts:
  U1 = ESP32-38PinWide [part_number=ESP32-38PinWide]
  A1 = 1 chan 3v relay module
  A2 = 1 chan 3v relay module
  A3 = 1 chan 3v relay module
  S5 = Round Pushbutton
  S6 = Round Pushbutton
  S7 = Round Pushbutton

nets:
  N1: U1.3.3, A1.pin_1, A2.pin_1, A3.pin_1
  N2: U1.GND, A1.pin_3, A2.pin_3, A3.pin_3
  N3: U1.GPIO16, A1.pin_2
  N4: U1.GPIO17, A3.pin_2
  N5: U1.GPIO5, A2.pin_2
  N6: A1.pin_6, S5.leg1
  N7: A1.pin_7, S5.leg0
  N8: A2.pin_6, S6.leg1
  N9: A2.pin_7, S6.leg0
  N10: A3.pin_6, S7.leg1
  N11: A3.pin_7, S7.leg0

custom parts:
  ESP32-38PinWide: Generic 38-Pin ESP32 with wide format (only access to one side of pins on a breadboard) based on Stephen Lilley's HiLetgo ESP-WROOM-32 ESP32 ESP-32S Development Board.
  1 chan 3v relay module: Single 3V relay isolated drive control module High level drive board.
